// Logisim project connect4_circuit.circ as structural Verilog
module main (
  input  [1:0] in_1
);

  wire color_decoder_1_out_2, color_decoder_1_out_3, color_decoder_1_out_4;

  // RGBLED rgbled_1: pin names not known
  // RGBLED rgbled_2: pin names not known
  // RGBLED rgbled_3: pin names not known
  // RGBLED rgbled_4: pin names not known
  // RGBLED rgbled_5: pin names not known
  // RGBLED rgbled_6: pin names not known
  // RGBLED rgbled_7: pin names not known
  // RGBLED rgbled_8: pin names not known
  // RGBLED rgbled_9: pin names not known
  // RGBLED rgbled_10: pin names not known
  // RGBLED rgbled_11: pin names not known
  // RGBLED rgbled_12: pin names not known
  // RGBLED rgbled_13: pin names not known
  // RGBLED rgbled_14: pin names not known
  // RGBLED rgbled_15: pin names not known
  // RGBLED rgbled_16: pin names not known
  // RGBLED rgbled_17: pin names not known
  // RGBLED rgbled_18: pin names not known
  // RGBLED rgbled_19: pin names not known
  // RGBLED rgbled_20: pin names not known
  // RGBLED rgbled_21: pin names not known
  // RGBLED rgbled_22: pin names not known
  // RGBLED rgbled_23: pin names not known
  // RGBLED rgbled_24: pin names not known
  // RGBLED rgbled_25: pin names not known
  // RGBLED rgbled_26: pin names not known
  // RGBLED rgbled_27: pin names not known
  // RGBLED rgbled_28: pin names not known
  // RGBLED rgbled_29: pin names not known
  // RGBLED rgbled_30: pin names not known
  // RGBLED rgbled_31: pin names not known
  // RGBLED rgbled_32: pin names not known
  // RGBLED rgbled_33: pin names not known
  // RGBLED rgbled_34: pin names not known
  // RGBLED rgbled_35: pin names not known
  // RGBLED rgbled_36: pin names not known
  // RGBLED rgbled_37: pin names not known
  // RGBLED rgbled_38: pin names not known
  // RGBLED rgbled_39: pin names not known
  // RGBLED rgbled_40: pin names not known
  // RGBLED rgbled_41: pin names not known
  color_decoder color_decoder_1 (
    .in_1(in_1), .out_2(color_decoder_1_out_2), .out_3(color_decoder_1_out_3), .out_4(color_decoder_1_out_4));
  // RGBLED rgbled_42: pin names not known; wires that end beside it: color_decoder_1_out_3, color_decoder_1_out_2, color_decoder_1_out_4
endmodule

module state_decoder (
  input  [48:0] in_1
);
endmodule

module color_decoder (
  input  [1:0] in_1,
  output out_2,
  output out_3,
  output out_4
);

  not not_1 (out_2, in_1[1]);
  nor nor_1 (out_4, in_1[1], in_1[0]);

  assign out_3 = 1'b1;

  // Notes on the sheet:
  //   00 - empty
  //   10 - player 1
  //   01 - player 2
endmodule
